# Fritzing sketch pixelhunter (saved by Fritzing 0.9.2b)
breadboards: 1

parts:
  LM324 = Dual Op-Amp [package=dip08]
  Uno = Arduino Uno (Rev3)
  TEMD6010FX01 = S1133 Si Photodiode [package="8mm Ceramic [THT]"]
  R1 = Resistor [tolerance=±5% resistance=3M package="0402 [SMD]"]
  R2 = Resistor [tolerance=±5% resistance=10k package=THT]
  R3 = Resistor [tolerance=±5% resistance=100k package=THT]

nets:
  N1: LM324.A_OUT, LM324.B_+IN, R1.Pin_1
  N2: LM324.A_-IN, TEMD6010FX01.anode, R1.Pin_0
  GND: LM324.A_+IN, LM324.A_V-, Uno.GND, TEMD6010FX01.cathode, R2.Pin_0
  N3: LM324.B_-IN, R2.Pin_1, R3.Pin_0
  N4: LM324.B_OUT, Uno.A0, R3.Pin_1
  5V: LM324.A_V+, Uno.5V
